# Fritzing sketch Omnichord 2 (saved by Fritzing 1.0.1rc)
circuit board: 6.73101cm x 4.89655cm
breadboards: 1

parts:
  Q1 = NPN-Transistor [package="TO92 [THT]"]
  Q2 = NPN-Transistor [package="TO92 [THT]"]
  Q3 = NPN-Transistor [package="TO92 [THT]"]
  Q4 = NPN-Transistor [package="TO92 [THT]"]
  Q5 = NPN-Transistor [package="TO92 [THT]"]
  Q6 = NPN-Transistor [package="TO92 [THT]"]
  Q7 = NPN-Transistor [package="TO92 [THT]"]
  Q8 = NPN-Transistor [package="TO92 [THT]"]
  Q9 = NPN-Transistor [package="TO92 [THT]"]
  Q10 = NPN-Transistor [package="TO92 [THT]"]
  Q11 = NPN-Transistor [package="TO92 [THT]"]
  Q12 = NPN-Transistor [package="TO92 [THT]"]
  10K = Resistor [tolerance=±5% power=0.25 resistance=220 package=THT]
  10K_2 = Resistor [tolerance=±5% power=0.25 resistance=220 package=THT]
  10K_3 = Resistor [tolerance=±5% power=0.25 resistance=220 package=THT]
  10K_4 = Resistor [tolerance=±5% power=0.25 resistance=220 package=THT]
  10K_5 = Resistor [tolerance=±5% power=0.25 resistance=220 package=THT]
  10K_6 = Resistor [tolerance=±5% power=0.25 resistance=220 package=THT]
  10K_7 = Resistor [tolerance=±5% power=0.25 resistance=220 package=THT]
  10K_8 = Resistor [tolerance=±5% power=0.25 resistance=220 package=THT]
  10K_9 = Resistor [tolerance=±5% power=0.25 resistance=220 package=THT]
  10K_10 = Resistor [tolerance=±5% power=0.25 resistance=220 package=THT]
  10K_11 = Resistor [tolerance=±5% power=0.25 resistance=220 package=THT]
  10K_12 = Resistor [tolerance=±5% power=0.25 resistance=220 package=THT]
  220R = Resistor [tolerance=±5% power=0.25 resistance=220 package=THT]
  220R_2 = Resistor [tolerance=±5% power=0.25 resistance=220 package=THT]
  220R_3 = Resistor [tolerance=±5% power=0.25 resistance=220 package=THT]
  220R_4 = Resistor [tolerance=±5% power=0.25 resistance=220 package=THT]
  220R_5 = Resistor [tolerance=±5% power=0.25 resistance=220 package=THT]
  220R_6 = Resistor [tolerance=±5% power=0.25 resistance=220 package=THT]
  220R_7 = Resistor [tolerance=±5% power=0.25 resistance=220 package=THT]
  220R_8 = Resistor [tolerance=±5% power=0.25 resistance=220 package=THT]
  220R_9 = Resistor [tolerance=±5% power=0.25 resistance=220 package=THT]
  220R_10 = Resistor [tolerance=±5% power=0.25 resistance=220 package=THT]
  220R_11 = Resistor [tolerance=±5% power=0.25 resistance=220 package=THT]
  220R_12 = Resistor [tolerance=±5% power=0.25 resistance=220 package=THT]
  Arduino_Nano = Arduino Nano (Rev3.0)

nets:
  N1: Q1.E, Q2.E, Q3.E, Q4.E, Q5.E, Q6.E, Q7.E, Q8.E, Q9.E, Q10.E, Q11.E, Q12.E, 10K.Pin_0, 10K_2.Pin_0, 10K_3.Pin_0, 10K_4.Pin_0, 10K_5.Pin_0, 10K_6.Pin_0, 10K_7.Pin_0, 10K_8.Pin_0, 10K_9.Pin_0, 10K_10.Pin_0, 10K_11.Pin_0, 10K_12.Pin_0, Arduino_Nano.GND
  N2: Q1.B, 10K.Pin_1, 220R.Pin_0
  N3: Q2.B, 10K_2.Pin_1, 220R_2.Pin_0
  N4: Q3.B, 10K_3.Pin_1, 220R_3.Pin_0
  N5: Q4.B, 10K_4.Pin_1, 220R_4.Pin_0
  N6: Q5.B, 10K_5.Pin_1, 220R_5.Pin_0
  N7: Q6.B, 10K_6.Pin_1, 220R_6.Pin_0
  N8: Q7.B, 10K_7.Pin_1, 220R_7.Pin_0
  N9: Q8.B, 10K_8.Pin_1, 220R_8.Pin_0
  N10: Q9.B, 10K_9.Pin_1, 220R_9.Pin_0
  N11: Q10.B, 10K_10.Pin_1, 220R_10.Pin_0
  N12: Q11.B, 10K_11.Pin_1, 220R_11.Pin_0
  N13: Q12.B, 10K_12.Pin_1, 220R_12.Pin_0
  N14: 220R.Pin_1, Arduino_Nano.D2
  N15: 220R_2.Pin_1, Arduino_Nano.D3
  N16: 220R_3.Pin_1, Arduino_Nano.D4
  N17: 220R_4.Pin_1, Arduino_Nano.D5
  N18: 220R_5.Pin_1, Arduino_Nano.D6
  N19: 220R_6.Pin_1, Arduino_Nano.D7
  N20: 220R_7.Pin_1, Arduino_Nano.D8
  N21: 220R_8.Pin_1, Arduino_Nano.D9
  N22: 220R_9.Pin_1, Arduino_Nano.D10
  N23: 220R_10.Pin_1, Arduino_Nano.D11/MOSI
  N24: 220R_11.Pin_1, Arduino_Nano.D12/MISO
  N25: 220R_12.Pin_1, Arduino_Nano.D13/SCK

notes:
  GND
  1
  3
  9
  2
  5
  8
  7
  11
  6
  4
  12
  10
  VCC
