# Fritzing sketch Omnichord Schematic (saved by Fritzing 1.0.1rc)
breadboards: 1

parts:
  Arduino_Nano = Arduino Nano (Rev3.0)
  MPR121 = MPR121 Breakout
  2N7000 = Basic FET N-Channel [package="D2Pak [SMD]"]
  R1 = Resistor [tolerance=±5% power=0.25 resistance=220 package=THT]
  R2 = Resistor [tolerance=±5% power=0.25 resistance=10k package=THT]
  R3 = Resistor [tolerance=±5% power=0.25 resistance=220 package=THT]
  R4 = Resistor [tolerance=±5% power=0.25 resistance=220 package=THT]
  R5 = Resistor [tolerance=±5% power=0.25 resistance=220 package=THT]
  R6 = Resistor [tolerance=±5% power=0.25 resistance=220 package=THT]
  R7 = Resistor [tolerance=±5% power=0.25 resistance=220 package=THT]
  R8 = Resistor [tolerance=±5% power=0.25 resistance=220 package=THT]
  R9 = Resistor [tolerance=±5% power=0.25 resistance=220 package=THT]
  R10 = Resistor [tolerance=±5% power=0.25 resistance=220 package=THT]
  R11 = Resistor [tolerance=±5% power=0.25 resistance=220 package=THT]
  R12 = Resistor [tolerance=±5% power=0.25 resistance=220 package=THT]
  R14 = Resistor [tolerance=±5% power=0.25 resistance=220 package=THT]
  R15 = Resistor [tolerance=±5% power=0.25 resistance=10k package=THT]
  R16 = Resistor [tolerance=±5% power=0.25 resistance=10k package=THT]
  R17 = Resistor [tolerance=±5% power=0.25 resistance=10k package=THT]
  R18 = Resistor [tolerance=±5% power=0.25 resistance=10k package=THT]
  R19 = Resistor [tolerance=±5% power=0.25 resistance=10k package=THT]
  R20 = Resistor [tolerance=±5% power=0.25 resistance=10k package=THT]
  R21 = Resistor [tolerance=±5% power=0.25 resistance=10k package=THT]
  R22 = Resistor [tolerance=±5% power=0.25 resistance=10k package=THT]
  R23 = Resistor [tolerance=±5% power=0.25 resistance=10k package=THT]
  R24 = Resistor [tolerance=±5% power=0.25 resistance=10k package=THT]
  R25 = Resistor [tolerance=±5% power=0.25 resistance=10k package=THT]
  2N7000_2 = Basic FET N-Channel [package="D2Pak [SMD]"]
  2N7000_3 = Basic FET N-Channel [package="D2Pak [SMD]"]
  2N7000_4 = Basic FET N-Channel [package="D2Pak [SMD]"]
  2N7000_5 = Basic FET N-Channel [package="D2Pak [SMD]"]
  2N7000_6 = Basic FET N-Channel [package="D2Pak [SMD]"]
  2N7000_7 = Basic FET N-Channel [package="D2Pak [SMD]"]
  2N7000_8 = Basic FET N-Channel [package="D2Pak [SMD]"]
  2N7000_9 = Basic FET N-Channel [package="D2Pak [SMD]"]
  2N7000_10 = Basic FET N-Channel [package="D2Pak [SMD]"]
  2N7000_11 = Basic FET N-Channel [package="D2Pak [SMD]"]
  2N7000_12 = Basic FET N-Channel [package="D2Pak [SMD]"]

nets:
  Omnichord GND: Arduino_Nano.GND, MPR121.ADDR, MPR121.GND, 2N7000.source, R2.Pin_0, R15.Pin_0, R16.Pin_0, R17.Pin_0, R18.Pin_0, R19.Pin_0, R20.Pin_0, R21.Pin_0, R22.Pin_0, R23.Pin_0, R24.Pin_0, R25.Pin_0, 2N7000_2.source, 2N7000_3.source, 2N7000_4.source, 2N7000_5.source, 2N7000_6.source, 2N7000_7.source, 2N7000_8.source, 2N7000_9.source, 2N7000_10.source, 2N7000_11.source, 2N7000_12.source
  N1: Arduino_Nano.D2, R12.Pin_0
  N2: Arduino_Nano.D3, R11.Pin_0
  N3: Arduino_Nano.D4, R10.Pin_0
  N4: Arduino_Nano.D5, R9.Pin_0
  N5: Arduino_Nano.D6, R8.Pin_0
  N6: Arduino_Nano.D7, R1.Pin_0
  N7: Arduino_Nano.D8, R3.Pin_0
  N8: Arduino_Nano.D9, R4.Pin_0
  N9: Arduino_Nano.D10, R5.Pin_0
  N10: Arduino_Nano.D11/MOSI, R6.Pin_0
  N11: Arduino_Nano.D12/MISO, R7.Pin_0
  Omnichord +12V: Arduino_Nano.VIN
  N12: Arduino_Nano.A5, MPR121.SCL
  N13: Arduino_Nano.A4, MPR121.SDA
  3V3: Arduino_Nano.3V3, MPR121.3.3V
  N14: Arduino_Nano.D13/SCK, R14.Pin_0
  Pad 12 -: MPR121.ELE11
  Pad 11 -: MPR121.ELE10
  Pad 10 -: MPR121.ELE9
  Pad 9 -: MPR121.ELE8
  Pad 8 -: MPR121.ELE7
  Pad 7 -: MPR121.ELE6
  Pad 6 -: MPR121.ELE5
  Pad 5 -: MPR121.ELE4
  Pad 4 -: MPR121.ELE3
  Pad 3 -: MPR121.ELE2
  Pad 2 -: MPR121.ELE1
  Pad 1 -: MPR121.ELE0
  N15: 2N7000.Gate, R2.Pin_1, R12.Pin_1
  Omnichord Original Strumplate Connector: 2N7000.drain, 2N7000_2.drain, 2N7000_3.drain, 2N7000_4.drain, 2N7000_5.drain, 2N7000_6.drain, 2N7000_7.drain, 2N7000_8.drain, 2N7000_9.drain, 2N7000_10.drain, 2N7000_11.drain, 2N7000_12.drain
  N16: R1.Pin_1, R18.Pin_1, 2N7000_6.Gate
  N17: R3.Pin_1, R20.Pin_1, 2N7000_7.Gate
  N18: R4.Pin_1, R19.Pin_1, 2N7000_8.Gate
  N19: R5.Pin_1, R25.Pin_1, 2N7000_9.Gate
  N20: R6.Pin_1, R22.Pin_1, 2N7000_10.Gate
  N21: R7.Pin_1, R24.Pin_1, 2N7000_11.Gate
  N22: R8.Pin_1, R21.Pin_1, 2N7000_5.Gate
  N23: R9.Pin_1, R17.Pin_1, 2N7000_4.Gate
  N24: R10.Pin_1, R16.Pin_1, 2N7000_3.Gate
  N25: R11.Pin_1, R15.Pin_1, 2N7000_2.Gate
  N26: R14.Pin_1, R23.Pin_1, 2N7000_12.Gate

notes:
  Touch Sensitive Strumplate
